# Fritzing sketch Fire_detection_suppression_system (saved by Fritzing 0.9.3b)
circuit board: 8.46667cm x 5.64444cm
breadboards: 2

parts:
  U1 = ESP32-38PinWide [part_number=ESP32-38PinWide]
  Part1 = LCD1602-I2C
  KF-1 = KF-301 Relay [package=THT]
  Mini_Water_Pump_3-6VDC1 = Mini Water Pump 3-6VDC [part_number="Mini Water Pump 3-6VDC" chip_label=IC package="DIP (Dual Inline) [THT]"]
  S1 = KY-026
  VCC1 = Battery block 9V

nets:
  N1: U1.GPIO14, KF-1.signal
  N2: U1.GPIO11, Part1.GND, KF-1.ground, S1.pin2
  VIN: U1.VIN, Part1.VCC, KF-1.power, S1.pin3
  N3: U1.GPIO4, S1.pin4
  N4: U1.GPIO21, Part1.SDA
  N5: U1.GPIO23, Part1.SCL
  N6: KF-1.C, VCC1.+
  N7: KF-1.NO, Mini_Water_Pump_3-6VDC1.+M
  N8: Mini_Water_Pump_3-6VDC1.-M, VCC1.-

custom parts:
  ESP32-38PinWide: Generic 38-Pin ESP32 with wide format (only access to one side of pins on a breadboard) based on Stephen Lilley's HiLetgo ESP-WROOM-32 ESP32 ESP-32S Development Board.
  LCD1602-I2C: A standard character display, usually with 2x16 characters. Comes in many colors with LCM1602 IIC attached.
  KF-301 Relay: KF-301
  KY-026: ky-026 flame sensor module
